// Logisim project ControlUnit.circ as structural Verilog: 2 circuits, main circuit main
module main (
  input  [3:0] INSTRUCTION,
  output [2:0] ALU_OP,
  output REG_SELECT,
  output REG_LOAD,
  output MEM_WRITE
);
endmodule

module ControlUnit (
  input  in_1,
  input  in_2,
  input  [3:0] INSTRUCTION,
  input  in_4,
  input  in_5
);

  main main_1 ();  // open: ALU_OP, REG_SELECT, REG_LOAD, INSTRUCTION, MEM_WRITE
endmodule
